# Fritzing sketch ESP32 (saved by Fritzing 0.9.3b)

parts:
  M1 = DOIT Esp32 DevKit v1 (30 pins long, 11 pins width) [part_number=ESP32S-PIN30]
  Part1 = RFID USB Reader
  L1 = Solenoid  # not connected
  KY-1 = Keyes Relay [package=THT]
  VCC1 = 4 x AAA Battery Mount
  PIR1 = PIR sensor

nets:
  3V3: M1.3V3, Part1.VCC, PIR1.VDD
  GND: M1.GND, Part1.TX-O, KY-1.ground, VCC1.-, PIR1.GND
  N1: M1.D4, Part1.GND
  N2: M1.D18, Part1.CP
  N3: M1.D19, Part1.ANT1
  N4: M1.D22, KY-1.signal
  N5: M1.D23, Part1.ANT2
  N6: M1.D34, PIR1.SIG
  N7: M1.D26, Part1.GNDT
  N8: M1.VIN, KY-1.power, KY-1.C, VCC1.+

custom parts:
  DOIT Esp32 DevKit v1 (30 pins long, 11 pins width): The DOIT Esp32 DevKit v1 is one of the development board created by DOIT to evaluate the ESP-WROOM-32 module. It is based on the ESP32 microcontroller that boasts Wifi, Bluetooth, Ethernet and Low Power support all in a single chip. (vanepp) made breadboard work, adjusted pin numbering and labels and reduced size of schematic and cleaned up pcb. This chip is 30pins long (2 x15) and 11 pins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
  Keyes Relay: The Keyes 5V relay module is suitable for SCM development, home appliance control. It uses a 5V~12V TIL control signal which can control DC / AC signal.
