# Fritzing sketch ESP8266 (saved by Fritzing 0.9.3b)

parts:
  U1 = NodeMCU V1.0
  2_Channel_Relay1 = 2 Channel Power Relay
  VCC1 = 4 x AAA Battery Mount
  DHT1 = DHT11 Humitidy and Temperature Sensor
  Part3 = Lilypad Battery Connect  # not connected
  Part4 = Lilypad Battery Connect
  LED1 = LEDs [package=led10mm]

nets:
  N1: U1.D2, DHT1.DATA
  3V3: U1.3V3, 2_Channel_Relay1.VCC#14, DHT1.VDD
  GND: U1.GND, 2_Channel_Relay1.GND, VCC1.-, DHT1.GND
  N2: U1.D6, 2_Channel_Relay1.IN1
  N3: U1.D7, 2_Channel_Relay1.IN2
  N4: U1.Vin, 2_Channel_Relay1.JD-VCC, 2_Channel_Relay1.VCC#9, VCC1.+
  N5: 2_Channel_Relay1.K1-COM, Part4.+
  N6: 2_Channel_Relay1.K1-NO, LED1.A
  N7: Part4.-, LED1.C

notes:
  220V AC

custom parts:
  NodeMCU V1.0: ESP8266 based NodeMCU
  2 Channel Power Relay: A 2 channel power relay. The module operates at 5V.
  DHT11 Humitidy and Temperature Sensor: DHT11 Humidity and Temperature Sensor
  Lilypad Battery Connect: The LilyPad Battery Connect simply gives you a connection point for a battery or anything else you might want to plug in to your LilyPad system. It consists of a single 2-pin JST connector on a small LilyPad board with positive and negative terminals. LilyPad is a wearable e-textile technology developed by Leah Buechley and cooperatively designed by Leah and SparkFun. Each LilyPad was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
